# Fritzing sketch photoradar (saved by Fritzing 1.0.7)
breadboards: 1

parts:
  Part1 = Arduino Uno (Rev3) - ICSP
  R1 = Resistor [tolerance=±1% resistance=10k package="2010 [SMD]"]
  Q1 = LTR-301 [package=ltr-301]
  J1 = Basic Servo
  part = Electrolytic Capacitor [capacitance=100µF voltage=35V package="200 mil [THT, electrolytic]"]

nets:
  N1: Part1.A0, R1.Pin_0, Q1.E
  GND: Part1.GND, R1.Pin_1, J1.gnd, part.-
  N2: Part1.D3_PWM, J1.pulse
  5V: Part1.5V, Q1.C, J1.vcc, part.+
